# Fritzing sketch Untitled Sketch 2 (saved by Fritzing 0.9.3b)
breadboards: 1

parts:
  Part1 = prefix0000
  R1 = Photocell (LDR) [package=THT]
  R2 = Resistor [tolerance=±5% resistance=1k package="2512 [SMD]"]
  R3 = Resistor [tolerance=±5% resistance=220 package="0805 [SMD]"]
  LED1 = smd LED [color="Red (633nm)" package="1206 [SMD]"]

nets:
  N1: Part1.3.3V, R1.pin_0
  N2: Part1.IO36, R1.pin_1, R2.Pin_0
  N3: Part1.GND, R2.Pin_1, LED1.cathode
  N4: Part1.IO22, R3.Pin_0
  N5: R3.Pin_1, LED1.anode
