# Fritzing sketch Motor_Driver (saved by Fritzing 0.9.3b)
breadboards: 1

parts:
  Part1 = prefix0000
  L298N1 = L298N DC motor driver
  M1 = DC Motor  # not connected

nets:
  N1: Part1.IO25, L298N1.IN2
  N2: Part1.IO26, L298N1.IN1
  N3: Part1.IO27, L298N1.ENA
  5V: Part1.5V, L298N1.12V
  GND: Part1.GND, L298N1.GND

custom parts:
  L298N DC motor driver: 2x DC motor driver with 78M05 positive voltage regulator (7..35 V) L298N: max 46 V, 2 A Set 5 V Enable jumper to enable 5 V regultor (needed for the L298N) and +5 V output at screw terminal or supply external +5 V at screw terminal Set ENA and/or ENB to +5 V to enable motor permanently or supply ENA and/or ENB with PWM signal IN1 and IN2 set rotation directory for motor A (OUT1/OUT2) IN2 and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
