# Fritzing sketch Multitasking (saved by Fritzing 0.9.3b)
breadboards: 1

parts:
  Part1 = prefix0000
  LED1 = LED - 5mm [color="Green (560nm)" package="5 mm [THT]"]
  LED2 = LED - 5mm [color="Yellow (595nm)" package="5 mm [THT]"]
  R1 = Resistor [tolerance=±5% resistance=100 package=THT]
  R2 = Resistor [tolerance=±5% resistance=100 package=THT]

nets:
  N1: Part1.GND, R1.Pin_1, R2.Pin_1
  N2: Part1.IO23, LED2.anode
  N3: Part1.IO22, LED1.anode
  N4: LED1.cathode, R1.Pin_0
  N5: LED2.cathode, R2.Pin_0
